# Fritzing sketch Schema (saved by Fritzing 0.9.3b)
breadboards: 1

parts:
  R1 = Resistor [tolerance=±5% resistance=1M package=THT]
  LED1 = LED - 5mm [color="Red (633nm)" package="5 mm [THT]"]
  L1 = Inductor [package="400 mil [THT]"]
  R2 = Resistor [tolerance=±5% resistance=10k package=THT]
  Composant1 = Arduino Uno (Rev3)
  R3 = Resistor [tolerance=±5% resistance=220 package=THT]
  U1 = TOUCH [package=touch1]
  C2 = Ceramic Capacitor [capacitance=0.1nF package="100 mil [THT, multilayer]"]
  C3 = Ceramic Capacitor [capacitance=10nF package="100 mil [THT, multilayer]"]
  R4 = Resistor [tolerance=±5% resistance=100 package=THT]
  R5 = Resistor [tolerance=±5% resistance=100 package=THT]
  R6 = Resistor [tolerance=±5% resistance=100 package=THT]
  LED2 = LED - 3mm [color="Red (633nm)" package="3 mm [THT]"]
  LED3 = LED - 3mm [color="Green (570nm)" package="3 mm [THT]"]
  LED4 = LED - 3mm [color="Blue (525nm)" package="3 mm [THT]"]

nets:
  N1: R1.Pin_0, Composant1.GND, R3.Pin_1, C3.0, LED2.cathode, LED3.cathode, LED4.cathode
  N2: LED1.cathode, C3.1
  N3: LED1.anode, L1.pin_0
  N4: L1.pin_1, R2.Pin_0, C2.1
  N5: R2.Pin_1, Composant1.D9_PWM, R3.Pin_0
  N6: Composant1.D5_PWM, R6.Pin_0
  N7: Composant1.D6_PWM, R5.Pin_0
  N8: Composant1.D7, R4.Pin_0
  N9: U1.T2, C2.0
  N10: R4.Pin_1, LED2.anode
  N11: R5.Pin_1, LED3.anode
  N12: R6.Pin_1, LED4.anode
